// Logisim project Proiect_Bancomat_Final.circ as structural Verilog
module main (
  input  Input_1,
  input  [1:0] Input_bus_1,
  input  switch2,
  input  Input_2,
  input  [1:0] Input_bus_2,
  input  [1:0] Input_bus_3,
  input  [1:0] Input_bus_4,
  input  [1:0] Input_bus_5,
  input  buton1,
  input  buton2,
  input  [1:0] Input_bus_6,
  input  switch,
  output Stare_D,
  output Stare_C,
  output Stare_B,
  output Output_2,
  output Stare_A,
  output Output_1,
  output M_Begin,
  output Output_3,
  output Output_4,
  output [3:0] Output_bus_11
);

  wire clock_1_out, delayer_1_output, div_frecv_1_clk_out, ram_pin_1_finded, sau_1bit_1_output,
       scazator_retragere_1_succes, sumator_depunere_1_succes, uc_1_en_afisor, uc_1_en_comp,
       uc_1_en_ram_papers, uc_1_en_ram_pin, uc_1_en_ram_sold, uc_1_en_scz, uc_1_en_sum, uc_1_mode;
  wire [1:0] ram_pin_1_position;
  wire [6:0] afisor_structural_1_output_afisor;
  wire [7:0] citire_pin_1_output;
  wire [9:0] convertor_suma_2_output, convertor_suma_5_output;
  wire [11:0] citire_bancnote_1_output, ram_sold_bancnote_1_output, ram_sold_cont_1_output,
       sau_12biti_1_output, sau_12biti_2_output, scazator_retragere_1_out_ram_banc,
       scazator_retragere_1_out_ram_cont, sumator_depunere_1_out_ram_banc, sumator_depunere_1_out_ram_util;

  Clock clock_1 (.out(clock_1_out));
  debouncer debouncer_2 (.buton(buton2), .clk(clock_1_out), .iesire(Output_4));
  not1 not1_1 (.\input (ram_pin_1_finded), .\output (Output_1));
  div_frecv div_frecv_1 (.clk(clock_1_out), .clk_out(div_frecv_1_clk_out));
  debouncer debouncer_1 (.buton(buton1), .clk(clock_1_out), .iesire(Output_3));
  citire_bancnote citire_bancnote_1 (
    .button(Output_4), .bancnota(Input_bus_6), .ok(switch), .\output (citire_bancnote_1_output));
  delayer delayer_1 (.Input(div_frecv_1_clk_out), .Output(delayer_1_output));
  UC uc_1 (
    .clock(div_frecv_1_clk_out), .reset(Input_1), .selectie(Input_bus_1), .urm(switch2), .rez_comp(Output_2),
    .rez_ver_PIN(Output_1), .Ok_PIN(ram_pin_1_finded), .Confirm_sel(Input_2), .Confirm_PIN(Output_3),
    .Confirm_sum(switch), .En_comp(uc_1_en_comp), .En_RAM_papers(uc_1_en_ram_papers), .EN_scz(uc_1_en_scz),
    .En_sum(uc_1_en_sum), .En_Ram_Pin(uc_1_en_ram_pin), .EN_Ram_Sold(uc_1_en_ram_sold),
    .EN_Afisor(uc_1_en_afisor), .mode(uc_1_mode), .Starea_M(M_Begin), .Starea_A(Stare_A), .Starea_B(Stare_B),
    .Starea_C(Stare_C), .Starea_D(Stare_D));
  citire_PIN citire_pin_1 (
    .cifra1(Input_bus_2), .cifra2(Input_bus_3), .cifra3(Input_bus_4), .cifra4(Input_bus_5),
    .confirm_pin(Output_3), .\output (citire_pin_1_output));
  convertor_suma convertor_suma_5 (.\input (citire_bancnote_1_output), .\output (convertor_suma_5_output));
  RAM_sold_bancnote ram_sold_bancnote_1 (
    .clk(delayer_1_output), .enable(uc_1_en_ram_papers), .load(sau_12biti_2_output),
    .mode(sau_1bit_1_output), .\output (ram_sold_bancnote_1_output));
  RAM_sold_cont ram_sold_cont_1 (
    .clk(delayer_1_output), .enable(uc_1_en_ram_sold), .adress_ram(ram_pin_1_position),
    .load(sau_12biti_1_output), .mode(sau_1bit_1_output), .\output (ram_sold_cont_1_output));
  RAM_PIN ram_pin_1 (
    .clk(delayer_1_output), .enable(uc_1_en_ram_pin), .mode(uc_1_mode), .\input (citire_pin_1_output),
    .finded(ram_pin_1_finded), .position(ram_pin_1_position));
  comparator_10 comparator_10_1 (
    .enable(uc_1_en_comp), .A(convertor_suma_5_output), .B(convertor_suma_2_output), .posibil(Output_2));
  afisor_structural afisor_structural_1 (
    .clk(clock_1_out), .enable(uc_1_en_afisor), .\input (convertor_suma_2_output),
    .output_afisor(afisor_structural_1_output_afisor), .output_mux(Output_bus_11));
  _7_Segment_Display L_7_Segment_Display_1 (
    .g(afisor_structural_1_output_afisor[0]), .f(afisor_structural_1_output_afisor[1]),
    .a(afisor_structural_1_output_afisor[6]), .b(afisor_structural_1_output_afisor[5]),
    .e(afisor_structural_1_output_afisor[2]), .d(afisor_structural_1_output_afisor[3]),
    .c(afisor_structural_1_output_afisor[4]), .dp(1'b0));
  convertor_suma convertor_suma_2 (.\input (ram_sold_cont_1_output), .\output (convertor_suma_2_output));
  SAU_12Biti sau_12biti_1 (
    .Input1(scazator_retragere_1_out_ram_cont), .Input2(sumator_depunere_1_out_ram_util),
    .Output(sau_12biti_1_output));
  SAU_12Biti sau_12biti_2 (
    .Input1(scazator_retragere_1_out_ram_banc), .Input2(sumator_depunere_1_out_ram_banc),
    .Output(sau_12biti_2_output));
  scazator_retragere scazator_retragere_1 (
    .enable(uc_1_en_scz), .scz_banc(ram_sold_bancnote_1_output), .scz_cont_util(ram_sold_cont_1_output),
    .scz_de_scazut(citire_bancnote_1_output), .out_RAM_banc(scazator_retragere_1_out_ram_banc),
    .out_RAM_cont(scazator_retragere_1_out_ram_cont), .succes(scazator_retragere_1_succes));
  sumator_depunere sumator_depunere_1 (
    .enable(uc_1_en_sum), .sum_cont(ram_sold_cont_1_output), .sum_bancnote(ram_sold_bancnote_1_output),
    .sum_adunat(citire_bancnote_1_output), .out_RAM_banc(sumator_depunere_1_out_ram_banc),
    .out_RAM_util(sumator_depunere_1_out_ram_util), .succes(sumator_depunere_1_succes));
  SAU_1Bit sau_1bit_1 (
    .Input1(scazator_retragere_1_succes), .Input2(sumator_depunere_1_succes), .Output(sau_1bit_1_output));
endmodule

module test (
);

  main main_1 ();  // open: Input_1, Input_bus_1, switch2, Input_2, Input_bus_2, Input_bus_3, Input_bus_4, Input_bus_5, buton1, buton2, Input_bus_6, switch, Stare_D, Stare_C, Stare_B, Output_2, Stare_A, Output_1, M_Begin, Output_3, Output_4, Output_bus_11
endmodule

// VHDL entity comparator_10, as the project stores it:
--comparator 10 biti
LIBRARY ieee;
USE ieee.std_logic_1164.all;

ENTITY comparator_10 IS
  PORT (	enable: in std_logic;
  		A, B: in std_logic_vector(9 downto 0);
        	posibil: out std_logic
);
END comparator_10;


ARCHITECTURE Arch_comp_10 OF comparator_10 IS
BEGIN

    process(A, B, enable)
    begin
    	posibil<='0';
    	if(enable = '1') then
        	if(A > B) then
         	   	posibil<='0';
        	elsif (A = B) then
            	posibil<='1';
        	else
            	posibil<='1';
        	end if;
	end if;
    end process;
END Arch_comp_10;

// VHDL entity sumator_scazator, as the project stores it:
--sumator/scazator
LIBRARY ieee;
USE ieee.std_logic_1164.all;
USE ieee.std_logic_unsigned.all;


ENTITY sumator_scazator IS
    PORT (enable: in std_logic;
          a, b : in std_logic_vector(9 downto 0);
          sel : in std_logic;    --0 => +;     1 => -
          output : out std_logic_vector(9 downto 0)
    );
END sumator_scazator;


ARCHITECTURE arh OF sumator_scazator IS

BEGIN
    process(a, b, sel, enable)    
    begin
    	   if(enable = '1') then
        		if(sel = '0') then
            		output <= a + b;
        		else 
            		output <= a - b;
        		end if;
    	   end if;
    end process;
END arh;

// VHDL entity RAM_sold_bancnote, as the project stores it:
--ram sold bancnote
LIBRARY ieee;
USE ieee.std_logic_1164.all;
USE ieee.numeric_std.all;
USE ieee.std_logic_unsigned.all;


ENTITY RAM_sold_bancnote IS
    PORT (clk, enable : in std_logic;
       	load : in std_logic_vector(11 downto 0);
        	mode : in std_logic;    -- 0 => read;   1 => write
        	output : out std_logic_vector(11 downto 0)
       );
END RAM_sold_bancnote;
	
ARCHITECTURE arh OF RAM_sold_bancnote IS

    	type matrice is array (0 to 3) of std_logic_vector(2 downto 0); 

BEGIN
    	process(load, mode, enable, clk)
        	variable mem : matrice := ("001", "010", "000", "011");
        	variable aux : std_logic_vector(11 downto 0);
    	begin
    	if(clk = '1' and clk'event) then
    		if(enable = '1') then
     		if(mode = '0') then    --read
            		aux(11 downto 9) := mem(0);  
            		aux(8 downto 6) := mem(1); 
            		aux(5 downto 3) := mem(2);  
            		aux(2 downto 0) := mem(3);   
       	 	elsif (mode = '1') then --write
        			mem(0) := load(11 downto 9);
        			mem(1) := load(8 downto 6);
        			mem(2) := load(5 downto 3);
        			mem(3) := load(2 downto 0);
        		end if;
        		output <= aux;
        	end if;
   	end if;
   	end process;
    

END arh;

// VHDL entity RAM_PIN, as the project stores it:
--memorie ram PIN

LIBRARY ieee;
USE ieee.std_logic_1164.all;
USE ieee.numeric_std.all;
USE ieee.std_logic_unsigned.all;


ENTITY RAM_PIN IS
    PORT (clk, enable, mode: in std_logic;    -- switch
        	input: in std_logic_vector(7 downto 0); --citire ram
        	finded: out std_logic;
       	position: out std_logic_vector(1 downto 0));    
END RAM_PIN;

ARCHITECTURE arch OF RAM_PIN IS
    type matrice is array(0 to 3) of std_logic_vector(7 downto 0);
BEGIN

    process(mode, clk, input, enable)
        variable mem: matrice:=("00110110", "10000111", "11111010", "10110001");
        variable pozitie_veche: integer :=100;
        variable contor: integer :=0;
        variable succesful: std_logic :='0';
    begin
            if(enable = '1') then
            	if(clk'event and clk='1') then
            		succesful := '0';
                	if(mode = '0') then
                		for i in 0 to 3 loop
	            			if(mem(i) = input) then
	                    		succesful:='1';
	                 			pozitie_veche := i;
	                 		end if;
	                 	end loop;
                	elsif(mode = '1') then
	              	   	mem(pozitie_veche) := input; --scriere
	              	   	succesful := '0';
	              	end if;
            	end if;
            end if;
            finded <= succesful;
            position <= std_logic_vector(to_unsigned(pozitie_veche, 2));
    end process;
END arch;

// VHDL entity RAM_sold_cont, as the project stores it:
LIBRARY ieee;
USE ieee.std_logic_1164.all;
USE ieee.numeric_std.all;
USE ieee.std_logic_unsigned.all;

ENTITY RAM_sold_cont IS
     PORT (
     	clk, enable : in std_logic;
         	adress_ram: in std_logic_vector(1 downto 0);
        	load: in std_logic_vector(11 downto 0);
        	mode: in std_logic;  --0 => read, 1 => write
          output: out std_logic_vector(11 downto 0)
    );
END RAM_sold_cont;


ARCHITECTURE TypeArchitecture OF RAM_sold_cont IS
    	type matrice is array (0 to 3) of std_logic_vector(11 downto 0); 
BEGIN
   	process(adress_ram, load, mode, enable, clk)
    
    	variable mem : matrice := ("000001010000", "001011000100", "000010000001", "001011001001");
    	begin
    		if(clk = '1' and clk'event) then
    			if(enable = '1') then
        			if(mode = '0') then 
            			output <= mem(conv_integer(adress_ram));  --read
        			elsif (mode = '1') then
            			mem(conv_integer(adress_ram)) := load; --write
        			end if;
       	 	end if;
    		end if;
    	end process;
END TypeArchitecture;

// VHDL entity UC, as the project stores it:
LIBRARY ieee;
USE ieee.std_logic_1164.all;
USE ieee.numeric_std.all;
USE ieee.std_logic_unsigned.all;

ENTITY UC IS
  PORT (clock, reset: in std_logic;
  	   selectie: in std_logic_vector(1 downto 0);
  	   urm : in std_logic;
	   rez_comp, rez_ver_PIN, Ok_PIN: in std_logic;
	   Confirm_sel, Confirm_PIN, Confirm_sum: in std_logic;
	   En_comp,En_RAM_papers, EN_scz, En_sum, En_Ram_Pin, EN_Ram_Sold, EN_Afisor, mode: out std_logic;
	   --error : out std_logic;
	   Starea_M, Starea_A, Starea_B, Starea_C, Starea_D: out std_logic);
END UC;

ARCHITECTURE UC_Architecture OF UC IS

	type states is (M_begin, M_Check_PIN, M_wait_sel, A_display, B_Wait_for_sum, B_Compare_account,
				 B_Substract, B_Delay, C_Wait_for_sum, C_Add_account, C_Delay , D_Enter_new_PIN, D_Verify_PIN, D_Modify_PIN);
	signal NX_STATE: states := M_begin;	
	signal STATE : states := M_begin;
BEGIN

UPDATE_STATE : process (reset, clock)
	begin			
		if (Reset = '1') then
			STATE <= M_begin;
		elsif (clock'EVENT and clock = '1') then
			STATE <= NX_STATE;
		end if;
	end process UPDATE_STATE;

TRANSITIONS: process(STATE, Confirm_sel, Confirm_PIN, Confirm_sum, rez_comp, rez_ver_PIN, Ok_PIN, urm)
	begin
		case STATE is 
			when M_begin => 	if(Confirm_PIN = '1') then
								NX_STATE <= M_Check_PIN;
							elsif(Confirm_PIN = '0') then
								NX_STATE <= M_begin;
							end if;
			when M_Check_PIN => if( Ok_PIN = '0') then 
								NX_STATE<=M_begin;
							elsif( Ok_PIN = '1') then 
								NX_STATE<=M_wait_sel;
							end if;
			when M_wait_sel => if( Confirm_sel = '0') then
								NX_STATE<=M_wait_sel;
							elsif (Confirm_sel = '1') then
								case selectie is
									when "00" => NX_STATE<=A_display;
									when "01" => NX_STATE<=B_Wait_for_sum;
									when "10" => NX_STATE<=C_Wait_for_sum;
									when others => NX_STATE<=D_Enter_new_PIN;
								end case;
							end if;
----------------------------------------------------A-------------------------------------------------------------------------------------------
			when A_Display => 	if(urm = '1') then 
								NX_STATE <= M_wait_sel;
						   	elsif(urm = '0') then
								NX_STATE <= A_Display;
							end if;
----------------------------------------------------B-------------------------------------------------------------------------------------------
			when B_Wait_for_sum => 	if(Confirm_sum = '1') then
									NX_STATE <= B_Compare_account;
								elsif(Confirm_sum = '0') then
									NX_STATE <= B_Wait_for_sum;
							   	end if;
			when B_Compare_account => if(rez_comp = '0') then
									NX_STATE<=M_begin;
								elsif(rez_comp = '1') then
									NX_STATE<=B_Substract;
								end if;
			when B_Substract => NX_STATE <= B_Delay;
			when B_Delay => 	if(urm = '1') then 
								NX_STATE <= M_wait_sel;
							elsif(urm = '0') then
								NX_STATE <= B_Delay;
							end if;
			
----------------------------------------------------C-------------------------------------------------------------------------------------------
			when C_Wait_for_sum => 	if(Confirm_sum = '1') then
									NX_STATE <= C_Add_account;
								elsif(Confirm_sum = '0') then
									NX_STATE <= C_Wait_for_sum;
							   	end if;
			when C_Add_account => NX_STATE <= C_Delay;
			when C_Delay => 	if(urm = '1') then
								NX_STATE <= M_wait_sel;
							elsif(urm = '0') then
								NX_STATE <= C_Delay;
							end if;
			
----------------------------------------------------D-------------------------------------------------------------------------------------------
			when D_Enter_new_PIN => if(Confirm_PIN = '1') then
									NX_STATE<= D_Verify_PIN;
								elsif(Confirm_PIN = '0') then
									NX_STATE<= D_Enter_new_PIN;
								end if;
			when D_Verify_PIN => 	if (Rez_ver_PIN = '0') then
									NX_STATE<=D_Enter_new_PIN;
								elsif (Rez_ver_PIN = '1') then
									NX_STATE<=D_Modify_PIN;
								end if;
			when D_Modify_PIN =>	if(urm = '1') then
									NX_STATE<=M_wait_sel;
								elsif(urm = '0') then
									NX_STATE<=D_Modify_PIN;
								end if;

			
			when others =>	NX_STATE<= M_begin;
		end case;							
	end process;

OUTPUT: process(STATE, rez_comp, rez_ver_PIN, Ok_PIN, urm)
	   begin 
			En_Ram_Pin <='0';
			En_Ram_Sold<='0';
			En_comp <='0';
			En_RAM_papers <='0';
			EN_scz <='0';
			EN_sum <='0';
			EN_Afisor <='0';
			mode <='0';
			Starea_M <='0';
			Starea_A <='0';
			Starea_B <='0';
			Starea_C <='0';
			Starea_D <='0';

			
	   		case STATE is
	   			when M_begin => Starea_M <='1';

				when M_Check_PIN => En_Ram_Pin<='1';
	   						 	mode <= '0';
	   						 	Starea_M <='1';
	  
	   			when A_display =>	En_Ram_Sold <='1';
	   						   	EN_Afisor <='1';
	   						   	mode <= '0';
								Starea_A <='1';

				when B_Wait_for_sum => Starea_B <='1';
				
	   			when B_Compare_account => En_comp <='1';
	   								 EN_Ram_Sold<='1';
							 		 Starea_B <='1';
		 
	   			when B_Substract => EN_scz <='1';
	   							En_RAM_papers<='1';
	   							EN_Ram_Sold<='1';
	   							En_Ram_Pin <='1';
	   							mode <= '0';
							 	Starea_B <='1';
	   							
	   			when B_Delay => 	EN_scz <='1';
	   							En_RAM_papers<='1';
	   							EN_Ram_Sold<='1';
							 	Starea_B <='1';

				when C_Wait_for_sum => Starea_C <='1';
	   						
	   			when C_Add_account =>	EN_sum <='1';
	   								En_RAM_papers<='1';
	   								EN_Ram_Sold<='1';
	   								mode <= '0';
							  		Starea_C <='1';

				when C_Delay => 	EN_sum <='1';
	   							En_RAM_papers<='1';
	   							EN_Ram_Sold<='1';
							  	Starea_C <='1';

				when D_Enter_new_PIN => Starea_D <='1';
	   					
	   			when D_Verify_PIN =>En_Ram_Pin<='1';
								Starea_D <='1';
	   			
	   			when D_Modify_PIN => En_Ram_Pin<='1';
	   							 mode <= '1';
								 Starea_D <='1';
	   							  
	   			when others => EN_Afisor <='0';
	   	end case;
	   end process;
END UC_Architecture;

// VHDL entity convertor_suma, as the project stores it:
--convertor date codificat intr-o suma
LIBRARY ieee;
USE ieee.std_logic_1164.all;
USE ieee.numeric_std.all;

ENTITY convertor_suma IS
  PORT (input : in std_logic_vector(11 downto 0);
        output : out std_logic_vector(9 downto 0)
);
END convertor_suma;

ARCHITECTURE TypeArchitecture OF convertor_suma IS

BEGIN
    process(input)
    variable sum : integer := 0;

    begin
        sum:=to_integer(unsigned(input(11 downto 9)))*500 + to_integer(unsigned(input(8 downto 6)))*100 + to_integer(unsigned(input(5 downto 3)))*50 + to_integer(unsigned(input(2 downto 0)))*10;
        output<= std_logic_vector(to_unsigned(sum, 10));
	end process;
END TypeArchitecture;

// VHDL entity citire_bancnote, as the project stores it:
LIBRARY ieee;
USE ieee.std_logic_1164.all;
USE ieee.numeric_std.all;

ENTITY citire_bancnote IS
  PORT (
		button: in std_logic;
  	   	bancnota: in std_logic_vector(1 downto 0);
  	   	output : out std_logic_vector(11 downto 0);
  	   	ok : in std_logic);
END citire_bancnote;

ARCHITECTURE arh1 OF citire_bancnote IS

signal out_cod: std_logic_vector(11 downto 0) :="000000000000";
BEGIN

	process(bancnota, ok, button)
	variable cnt500: integer := 0;
	variable cnt100: integer := 0;
	variable cnt50: integer := 0;
	variable cnt10: integer := 0;
	begin	
		case bancnota is
			when "00" => if(button = '1' and button'event) then
						   	cnt10:=cnt10+1;
					   out_cod(2 downto 0)<= std_logic_vector(to_unsigned(cnt10, 3));
					   end if;
			when "01" => if(button = '1' and button'event) then
						   	cnt50:=cnt50+1;
					   out_cod(5 downto 3)<= std_logic_vector(to_unsigned(cnt50, 3));
					   end if;
			when "10" => if(button = '1' and button'event) then
						   	cnt100:=cnt100+1;
					   out_cod(8 downto 6)<= std_logic_vector(to_unsigned(cnt100, 3));
					   end if;
			when others =>if(button = '1' and button'event) then
						   	cnt500:=cnt500+1; 
					    out_cod(11 downto 9)<= std_logic_vector(to_unsigned(cnt500, 3));
					    end if;
			end case;
		if(ok = '1') then
			output<=out_cod;
		elsif(ok = '0') then
			output<="000000000000";
		end if;
end process;

END arh1;

// VHDL entity citire_PIN, as the project stores it:
LIBRARY ieee;
USE ieee.std_logic_1164.all;

ENTITY citire_PIN IS
	PORT (
  		cifra1, cifra2, cifra3, cifra4 : in std_logic_vector(1 downto 0);
  		confirm_pin : in std_logic;
  		output : out std_logic_vector(7 downto 0)
    	);
END citire_PIN;


ARCHITECTURE arh OF citire_PIN IS

BEGIN
	process(cifra1, cifra2, cifra3, cifra4, confirm_pin)
		variable val : std_logic_vector(7 downto 0);
	begin

		val(7 downto 6) := cifra1;
		val(5 downto 4) := cifra2;
		val(3 downto 2) := cifra3;
		val(1 downto 0) := cifra4;
		if(confirm_pin = '1') then
			output <= val;
		end if;
	end process;

END arh;

// VHDL entity afisor_structural, as the project stores it:
LIBRARY ieee;
USE ieee.std_logic_1164.all;

ENTITY afisor_structural IS
	PORT (
		clk, enable : in std_logic;
  		input : in std_logic_vector(9 downto 0);
    		output_afisor : out std_logic_vector(6 downto 0);
    		output_mux : out std_logic_vector(3 downto 0) 		
    	);
END afisor_structural;


ARCHITECTURE arh_afisor_struct OF afisor_structural IS

	component counter_afisor_div IS
		PORT (
			clk , enable: in std_logic;
	  		out_cnt : out std_logic_vector(16 downto 0)
		);
	END component;

	component dcd_suma_afisor IS
		PORT (
			input : in std_logic_vector(9 downto 0);
			unit, zeci, sute, mii : out std_logic_vector(3 downto 0)
	    	);
	END component;

	component mux_anod_afisor IS
		PORT (
	 		sel : in std_logic_vector(1 downto 0);
	 		output: out std_logic_vector(3 downto 0)
		);
	END component;

	component mux_cifra_afisor IS
		PORT (
	  		input0, input1, input2, input3 : in std_logic_vector(3 downto 0);
	  		sel : in std_logic_vector(1 downto 0);
	  		output : out std_logic_vector(3 downto 0)
	    	);
	END component;

	component dcd_hexa_7seg_afisor IS
	  	PORT (
	  		input : in	 std_logic_vector(3 downto 0);
	  		output : out std_logic_vector(6 downto 0)
	    	);
	END component;
	
	signal s_unit, s_zeci, s_sute, s_mii : std_logic_vector(3 downto 0);
	signal s_out_cnt : std_logic_vector(16 downto 0);
	signal s_output_cifra_afisor : std_logic_vector(3 downto 0);
	
BEGIN
	p_counter_afisor : counter_afisor_div port map (clk, enable, s_out_cnt);
	
p_dcd_suma_afisor : dcd_suma_afisor port map (input, s_unit, s_zeci, s_sute, s_mii);
	p_mux_cifra_afisor : mux_cifra_afisor port map (s_unit, s_zeci, s_sute, s_mii, s_out_cnt(1 downto 0), s_output_cifra_afisor);
	p_dcd_hexa_7seg_afisor : dcd_hexa_7seg_afisor port map (s_output_cifra_afisor, output_afisor);
	p_mux_anod_afisor : mux_anod_afisor port map (s_out_cnt(1 downto 0), output_mux);
END arh_afisor_struct;


-------------------------------------------------------------------------------------------------------------------------------

LIBRARY ieee;
USE ieee.std_logic_1164.all;
USE ieee.std_logic_unsigned.all;


ENTITY counter_afisor_div IS
	PORT (
  		clk , enable: in std_logic;
  		out_cnt : out std_logic_vector(16 downto 0)
	);
END counter_afisor_div;


ARCHITECTURE arh_cnt OF counter_afisor_div IS

	signal cnt : std_logic_vector(16 downto 0) := "00000000000000000";
	signal div_clk: std_logic := '0';
	signal nr_div: integer := 1;
BEGIN
	process(clk, nr_div, enable)
	BEGIN
		if(enable = '1') then
			if(clk = '1' and clk'event) then 
				if(nr_div = 4) then
					nr_div <= 1;
				elsif(nr_div = 2) then 
					div_clk <= '0';
					nr_div <= nr_div + 1;
				else
					div_clk <= '1';
					nr_div <= nr_div + 1;
				end if;
			end if;
		end if;
	end process;

	
	process(div_clk, enable)
	begin
		if(enable = '1') then
			if(div_clk = '1' and div_clk'event) then 
				cnt <= cnt + 1;
			end if;
		end if;
	end process;
	out_cnt <= cnt;

END arh_cnt;
 
-------------------------------------------------------------------------------------------------------------------------------

LIBRARY ieee;
USE ieee.std_logic_1164.all;
USE ieee.std_logic_unsigned.all;
use ieee.numeric_std.all;
use ieee.numeric_std.all;

ENTITY dcd_suma_afisor IS
	PORT (
		input : in std_logic_vector(9 downto 0);
		unit, zeci, sute, mii : out std_logic_vector(3 downto 0)
    	);
END dcd_suma_afisor;


ARCHITECTURE arh_dcd OF dcd_suma_afisor IS

	signal a : natural;
BEGIN
	a <= conv_integer(input);
	unit <= std_logic_vector(to_unsigned(a rem 10, 4));
	zeci <= std_logic_vector(to_unsigned(a/10 rem 10, 4));
	sute <= std_logic_vector(to_unsigned(a/100 rem 10, 4));
	mii <= std_logic_vector(to_unsigned(a/1000 rem 10, 4));
END arh_dcd;

-------------------------------------------------------------------------------------------------------------------------------

LIBRARY ieee;
USE ieee.std_logic_1164.all;

ENTITY mux_anod_afisor IS
	PORT (
 		sel : in std_logic_vector(1 downto 0);
 		output: out std_logic_vector(3 downto 0)
	);
END mux_anod_afisor;


ARCHITECTURE arh_mux_anod OF mux_anod_afisor IS

BEGIN

	process(sel)
	begin
		case sel is
			when "00" => output <= "0001";
			when "01" => output <= "0010";
			when "10" => output <= "0100";
			when others => output <= "1000";

		end case;
	end process;
END arh_mux_anod;

-------------------------------------------------------------------------------------------------------------------------------

LIBRARY ieee;
USE ieee.std_logic_1164.all;

ENTITY mux_cifra_afisor IS
	PORT (
  		input0, input1, input2, input3 : in std_logic_vector(3 downto 0);
  		sel : in std_logic_vector(1 downto 0);
  		output : out std_logic_vector(3 downto 0)
    	);
END mux_cifra_afisor;


ARCHITECTURE arh_mux_cifra OF mux_cifra_afisor IS

BEGIN

	process(sel, input0, input1, input2, input3)
	begin
		case sel is
			when "00" => output <= input0;
			when "01" => output <= input1;
			when "10" => output <= input2;
			when others => output <= input3;

		end case;
	end process;

END arh_mux_cifra;

-------------------------------------------------------------------------------------------------------------------------------

LIBRARY ieee;
USE ieee.std_logic_1164.all;

ENTITY dcd_hexa_7seg_afisor IS
  	PORT (
  		input : in std_logic_vector(3 downto 0);
  		output : out std_logic_vector(6 downto 0)
    	);
END dcd_hexa_7seg_afisor;


ARCHITECTURE arh_7seg OF dcd_hexa_7seg_afisor IS

BEGIN

	output <= 	"1111110" when input = x"0" else
				"0110000" when input = x"1" else
				"1101101" when input = x"2" else
				"1111001" when input = x"3" else
				"0110011" when input = x"4" else
				"1011011" when input = x"5" else
				"1011111" when input = x"6" else
				"1110000" when input = x"7" else
				"1111111" when input = x"8" else
				"1111011" when input = x"9" else
				"1110111" when input = x"A" else
				"0011111" when input = x"B" else
				"1001110" when input = x"C" else
				"0111101" when input = x"D" else
				"1001111" when input = x"E" else
				"1000111" when input = x"F"; 
END arh_7seg;

// VHDL entity scazator_retragere, as the project stores it:
--scazator
LIBRARY ieee;
USE ieee.std_logic_1164.all;
USE ieee.numeric_std.all;


ENTITY scazator_retragere IS
  PORT (enable: in std_logic;
  	   scz_banc: in std_logic_vector(11 downto 0);
  	   scz_cont_util: in std_logic_vector(11 downto 0);
  	   scz_de_scazut: in std_logic_vector(11 downto 0);
  	   out_RAM_banc: out std_logic_vector(11 downto 0);
  	   out_RAM_cont: out std_logic_vector(11 downto 0);
  	   succes: out std_logic);
END scazator_retragere;

ARCHITECTURE TypeArchitecture OF scazator_retragere IS
BEGIN
	process(enable, scz_banc, scz_de_scazut)
	variable var_500: integer := 0;
     variable var_100: integer := 0;
     variable var_50: integer := 0;
     variable var_10: integer := 0;
     variable cmp2, cmp1: integer:=0;
     variable ok: std_logic:='1';
     variable sum: std_logic_vector(11 downto 0):="000000000000";
	begin
		out_RAM_banc <="000000000000";
		out_RAM_cont <="000000000000";
		succes <= '0';
		if(enable = '1') then
				cmp2:=to_integer(unsigned(scz_banc(11 downto 9)))*500 + to_integer(unsigned(scz_banc(8 downto 6)))*100 + to_integer(unsigned(scz_banc(5 downto 3)))*50 + to_integer(unsigned(scz_banc(2 downto 0)))*10;
				cmp1:=to_integer(unsigned(scz_de_scazut(11 downto 9)))*500 + to_integer(unsigned(scz_de_scazut(8 downto 6)))*100 + to_integer(unsigned(scz_de_scazut(5 downto 3)))*50 + to_integer(unsigned(scz_de_scazut(2 downto 0)))*10;
			
				if(cmp2 >= cmp1) then -- cand suma adunata in RAM_banc este mai mare decat ce cere utilizatorul 
					succes<='1';
					var_500:=to_integer(unsigned(scz_banc(11 downto 9)))- to_integer(unsigned(scz_de_scazut(11 downto 9)));
					var_100:=to_integer(unsigned(scz_banc(8 downto 6)))- to_integer(unsigned(scz_de_scazut(8 downto 6)));
					var_50:=to_integer(unsigned(scz_banc(5 downto 3)))- to_integer(unsigned(scz_de_scazut(5 downto 3)));
					var_10:=to_integer(unsigned(scz_banc(2 downto 0)))- to_integer(unsigned(scz_de_scazut(2 downto 0)));

					
					for i in 0 to 6 loop
						if(var_500 < 0) then
							var_100:=var_100 - 5;
							var_500:=var_500 + 1;
						end if;
						end loop;
					if(var_500 < 0) then
						ok := '0';
					end if;
					
					for i in 0 to 6 loop
						if(var_100 < 0) then
							var_100:=var_100 +1;
							var_50:=var_50 - 2;
						end if;
					end loop;
					if(var_100 < 0) then
						ok := '0';
					end if;
					
					for i in 0 to 6 loop
						if(var_50 < 0) then
							var_50:=var_50 +1;
							var_10:=var_10 - 5;
						end if;
					end loop;
					if(var_50 < 0) then
						ok := '0';
					end if;

					if(var_10 < 0) then
						ok := '0';
					end if;
	
				sum(11 downto 9):= std_logic_vector(to_unsigned(var_500, 3));
				sum(8 downto 6):= std_logic_vector(to_unsigned(var_100, 3));
				sum(5 downto 3):= std_logic_vector(to_unsigned(var_50, 3));
				sum(2 downto 0):= std_logic_vector(to_unsigned(var_10, 3));
			
				if(ok ='1') then
					out_RAM_banc<= sum;
					succes<='1';

					var_500:=to_integer(unsigned(scz_cont_util(11 downto 9)))- to_integer(unsigned(scz_de_scazut(11 downto 9)));
					var_100:=to_integer(unsigned(scz_cont_util(8 downto 6)))- to_integer(unsigned(scz_de_scazut(8 downto 6)));
					var_50:=to_integer(unsigned(scz_cont_util(5 downto 3)))- to_integer(unsigned(scz_de_scazut(5 downto 3)));
					var_10:=to_integer(unsigned(scz_cont_util(2 downto 0)))- to_integer(unsigned(scz_de_scazut(2 downto 0)));

					sum(11 downto 9):= std_logic_vector(to_unsigned(var_500, 3));
					sum(8 downto 6):= std_logic_vector(to_unsigned(var_100, 3));
					sum(5 downto 3):= std_logic_vector(to_unsigned(var_50, 3));
					sum(2 downto 0):= std_logic_vector(to_unsigned(var_10, 3));
					out_RAM_cont<=sum;
					
				else
					out_RAM_banc <=scz_banc;
					out_RAM_cont <=scz_cont_util;
					succes<='0';
				end if;
			else
				out_RAM_banc <= scz_banc;
				out_RAM_banc<=scz_cont_util;
				succes<='0';
			end if;
		end if;
	end process;
END TypeArchitecture;

// VHDL entity sumator_depunere, as the project stores it:
--sumator
LIBRARY ieee;
USE ieee.std_logic_1164.all;

USE ieee.numeric_std.all;
ENTITY sumator_depunere IS
  PORT (enable: in std_logic;
  	   sum_cont: in std_logic_vector(11 downto 0);
  	   sum_bancnote: in std_logic_vector(11 downto 0);
  	   sum_adunat: in std_logic_vector(11 downto 0);
  	   out_RAM_banc: out std_logic_vector(11 downto 0);
  	   out_RAM_util: out std_logic_vector(11 downto 0);
  	   succes: out std_logic
  	   );
END sumator_depunere;



ARCHITECTURE TypeArchitecture OF sumator_depunere IS

BEGIN

	process(enable, sum_cont, sum_bancnote, sum_adunat)
	variable var_500: integer := 0;
     variable var_100: integer := 0;
     variable var_50: integer := 0;
     variable var_10: integer := 0;
     variable sum: std_logic_vector(11 downto 0):="000000000000";
	begin
		succes <= '0';
		if(enable = '1') then 
			var_500:=to_integer(unsigned(sum_cont(11 downto 9)))+ to_integer(unsigned(sum_adunat(11 downto 9)));
			var_100:=to_integer(unsigned(sum_cont(8 downto 6)))+ to_integer(unsigned(sum_adunat(8 downto 6)));
			var_50:=to_integer(unsigned(sum_cont(5 downto 3)))+ to_integer(unsigned(sum_adunat(5 downto 3)));
			var_10:=to_integer(unsigned(sum_cont(2 downto 0)))+ to_integer(unsigned(sum_adunat(2 downto 0)));
			sum(11 downto 9):= std_logic_vector(to_unsigned(var_500, 3));
			sum(8 downto 6):= std_logic_vector(to_unsigned(var_100, 3));
			sum(5 downto 3):= std_logic_vector(to_unsigned(var_50, 3));
			sum(2 downto 0):= std_logic_vector(to_unsigned(var_10, 3));

			out_RAM_util<=sum;

			var_500:=to_integer(unsigned(sum_bancnote(11 downto 9)))+ to_integer(unsigned(sum_adunat(11 downto 9)));
			var_100:=to_integer(unsigned(sum_bancnote(8 downto 6)))+ to_integer(unsigned(sum_adunat(8 downto 6)));
			var_50:=to_integer(unsigned(sum_bancnote(5 downto 3)))+ to_integer(unsigned(sum_adunat(5 downto 3)));
			var_10:=to_integer(unsigned(sum_bancnote(2 downto 0)))+ to_integer(unsigned(sum_adunat(2 downto 0)));
			sum(11 downto 9):= std_logic_vector(to_unsigned(var_500, 3));
			sum(8 downto 6):= std_logic_vector(to_unsigned(var_100, 3));
			sum(5 downto 3):= std_logic_vector(to_unsigned(var_50, 3));
			sum(2 downto 0):= std_logic_vector(to_unsigned(var_10, 3));

			out_RAM_banc<=sum;
			succes <= '1';
		else
			out_RAM_banc<="000000000000";
			out_RAM_util<="000000000000";
			succes <= '0';
		end if;

	end process;
END TypeArchitecture;

// VHDL entity delayer, as the project stores it:
LIBRARY ieee;
USE ieee.std_logic_1164.all;

ENTITY delayer IS
  PORT (Input: in std_logic;
  	   Output: out std_logic);
END delayer;

ARCHITECTURE TypeArchitecture OF delayer IS
BEGIN
	process(Input)
	begin
		if( Input = '1') then
			Output<='1' after 100 ns;
		else
			Output<='0' after 100 ns;
		end if;
	end process;
END TypeArchitecture;

// VHDL entity SAU_1Bit, as the project stores it:
LIBRARY ieee;
USE ieee.std_logic_1164.all;

ENTITY SAU_1Bit IS
  PORT (Input1, Input2: in std_logic;
  	   Output: out std_logic);
END SAU_1Bit;

ARCHITECTURE TypeArchitecture OF SAU_1Bit IS

BEGIN
	Output<=Input1 or Input2;

END TypeArchitecture;

// VHDL entity SAU_12Biti, as the project stores it:
LIBRARY ieee;
USE ieee.std_logic_1164.all;

ENTITY SAU_12Biti IS
  PORT (Input1, Input2: in std_logic_vector(11 downto 0);
  	   Output: out std_logic_vector(11 downto 0));
END SAU_12Biti;

ARCHITECTURE TypeArchitecture OF SAU_12Biti IS

BEGIN
	Output<=Input1 or Input2;

END TypeArchitecture;

// VHDL entity debouncer, as the project stores it:
LIBRARY ieee;
USE ieee.std_logic_1164.all;

ENTITY debouncer IS
  PORT (
 buton, clk: in std_logic;
         iesire: out std_logic
    );
END debouncer;

ARCHITECTURE TypeArchitecture OF debouncer IS
BEGIN
    process(buton, clk)
    variable num: integer:=0;
    begin 
    if(buton='1') then
         if(rising_edge(clk)) then num:=num+1;
         end if;
    else num:=0;
    end if;

    if(num>15) then iesire<='1';
    else iesire<='0';
        end if;
    end process;  
END TypeArchitecture;

// VHDL entity div_frecv, as the project stores it:
LIBRARY ieee;
USE ieee.std_logic_1164.all;
USE ieee.std_logic_unsigned.all;


ENTITY div_frecv IS
	PORT (
  		clk : in std_logic;
  		clk_out : out std_logic
	);
END div_frecv;

ARCHITECTURE arh_cnt OF div_frecv IS

	signal clk_div: std_logic := '0';
	signal cnt: integer := 0;
BEGIN
	process(clk, cnt)
	BEGIN
		if(clk = '1' and clk'event) then 
				if(cnt = 2) then
					cnt <= 1;
					clk_div <= not clk_div;
				else 
					cnt <= cnt+1;
				end if;
		end if;
	end process;
	clk_out <= clk_div;

END arh_cnt;

// VHDL entity not1, as the project stores it:
LIBRARY ieee;
USE ieee.std_logic_1164.all;

ENTITY not1 IS
  PORT (input: in std_logic;
  	   output: out std_logic);
END not1;

ARCHITECTURE TypeArchitecture OF not1 IS

BEGIN
	output<=not input;

END TypeArchitecture;
